// Logisim project trab_final.circ as structural Verilog: 1 circuit, main circuit main
module main (
);

  wire and_1_out, and_2_out, and_3_out, and_4_out, and_5_out, and_6_out, and_7_out, and_8_out, and_9_out,
       and_10_out, and_11_out, and_12_out, B_out, clock_1_out, L_out, not_1_out, or_1_out, or_2_out,
       or_3_out, or_4_out, or_5_out, or_6_out, Q0_q, Q0_qn, Q1_q, Q1_qn, Q2_q, Q2_qn;

  Button L (.out(L_out));
  Button B (.out(B_out));
  not not_1 (not_1_out, B_out);
  Clock clock_1 (.out(clock_1_out));
  _7_Segment_Display u_7_segment_display_1 (.g(1'b1), .f(1'b1), .a(1'b1), .b(1'b1), .e(1'b1), .c(1'b1));  // open: d, dp
  _7_Segment_Display u_7_segment_display_2 (.f(1'b1), .a(1'b1), .e(1'b1), .d(1'b1));  // open: g, b, c, dp
  and and_1 (and_1_out, Q2_qn, L_out, not_1_out);
  and and_2 (and_2_out, Q1_q, Q0_q);
  and and_3 (and_3_out, Q1_q, Q0_q);
  or or_1 (or_1_out, Q0_q, and_1_out);
  or or_2 (or_2_out, Q1_q, B_out, Q2_q);
  _7_Segment_Display u_7_segment_display_3 (.f(1'b1), .a(1'b1), .b(1'b1), .e(1'b1), .d(1'b1), .c(1'b1));  // open: g, dp
  J_K_Flip_Flop Q2 (
    .J(and_2_out), .clk(clock_1_out), .K(and_3_out), .Q(Q2_q), .Qn(Q2_qn), .en(1'b1));  // open: preset, reset
  J_K_Flip_Flop Q1 (.J(or_1_out), .clk(clock_1_out), .K(Q0_q), .Q(Q1_q), .Qn(Q1_qn), .en(1'b1));  // open: preset, reset
  J_K_Flip_Flop Q0 (.J(or_2_out), .clk(clock_1_out), .K(1'b1), .Q(Q0_q), .Qn(Q0_qn), .en(1'b1));  // open: preset, reset
  _7_Segment_Display u_7_segment_display_4 (.g(1'b1), .f(1'b1), .a(1'b1), .b(1'b1), .e(1'b1));  // open: d, c, dp
  and and_4 (and_4_out, Q2_qn, Q1_q, Q0_qn);
  and and_5 (and_5_out, Q2_qn, Q1_qn, Q0_q);
  and and_6 (and_6_out, Q1_qn, Q0_qn);
  and and_7 (and_7_out, Q2_qn, Q1_q, Q0_q);
  and and_8 (and_8_out, Q2_q, Q1_qn);
  and and_9 (and_9_out, Q2_q, Q0_qn);
  or or_3 (or_3_out, and_4_out, and_5_out, and_10_out);
  and and_10 (and_10_out, Q2_q, Q1_q, Q0_q);
  or or_4 (or_4_out, Q2_q, Q0_qn, Q1_q);
  or or_5 (or_5_out, and_6_out, and_7_out, and_8_out, and_9_out);
  _7_Segment_Display u_7_segment_display_5 (
    .g(or_5_out), .f(1'b1), .a(1'b1), .b(or_4_out), .e(1'b1), .d(or_3_out), .c(or_6_out));  // open: dp
  or or_6 (or_6_out, and_11_out, and_12_out);
  and and_11 (and_11_out, Q0_qn, Q2_qn);
  and and_12 (and_12_out, Q2_q, Q1_q, Q0_q);

  // Notes on the sheet:
  //   Automoveis Ligado
  //   Peoes Desligado
  //   Amarelo
  //   Desligado
  //   Desligado
  //   Desligado
  //   Desligado
  //   Ligado
endmodule
